// Logisim project Project4Given.circ as structural Verilog: 16 circuits, main circuit main
module main (
  input  [3:0] in_1,
  input  [3:0] in_2,
  input  [3:0] in_3,
  input  [3:0] in_4,
  input  [3:0] in_5
);

  wire CLK, keyboard_1_avail, keyboard_2_avail, keyboarddriver_1_read, keyboarddriver_2_read,
       pull_resistor_1_node, ttydriver_1_write, ttydriver_2_write, ttydriver_3_write, vpwbmonitor_1_last_fe;
  wire [3:0] vpwbmonitor_1_last_addr;
  wire [6:0] keyboard_1_data, keyboard_2_data, ttydriver_1_data, ttydriver_2_data, ttydriver_3_data;
  wire [7:0] vpwbmonitor_1_last_data;
  wire [24:0] vpwbmonitor_1_out_4;
  wire [31:0] vpwbmonitor_1_out_3;

  Clock clock_1 (.out(CLK));
  Keyboard keyboard_1 (
    .clk(CLK), .re(keyboarddriver_1_read), .avail(keyboard_1_avail), .data(keyboard_1_data));  // open: clr
  Keyboard keyboard_2 (
    .clk(CLK), .re(keyboarddriver_2_read), .avail(keyboard_2_avail), .data(keyboard_2_data));  // open: clr
  Pull_Resistor #(.pull(1)) pull_resistor_1 (.node(pull_resistor_1_node));
  KeyboardDriver keyboarddriver_1 (
    .DATA(keyboard_1_data), .DEST(in_1), .DR(keyboard_1_avail), .CLK(CLK), .RXIN(pull_resistor_1_node),
    .READ(keyboarddriver_1_read), .TXOUT(pull_resistor_1_node));
  KeyboardDriver keyboarddriver_2 (
    .DATA(keyboard_2_data), .DEST(in_3), .DR(keyboard_2_avail), .CLK(CLK), .RXIN(pull_resistor_1_node),
    .READ(keyboarddriver_2_read), .TXOUT(pull_resistor_1_node));
  // Probe on vpwbmonitor_1_out_3
  VPWBMonitor vpwbmonitor_1 (
    .RXIN(pull_resistor_1_node), .CLK(CLK), .LAST_FE(vpwbmonitor_1_last_fe),
    .LAST_ADDR(vpwbmonitor_1_last_addr), .LAST_DATA(vpwbmonitor_1_last_data), .out_3(vpwbmonitor_1_out_3),
    .out_4(vpwbmonitor_1_out_4));
  TTY tty_1 (.data(ttydriver_1_data), .clk(CLK), .we(ttydriver_1_write));  // open: clr
  TTYDriver ttydriver_1 (
    .RXIN(pull_resistor_1_node), .CLK(CLK), .TTY_ADDR(in_2), .TXOUT(pull_resistor_1_node),
    .WRITE(ttydriver_1_write), .DATA(ttydriver_1_data));
  TTY tty_2 (.data(ttydriver_2_data), .clk(CLK), .we(ttydriver_2_write));  // open: clr
  TTYDriver ttydriver_2 (
    .RXIN(pull_resistor_1_node), .CLK(CLK), .TTY_ADDR(in_4), .TXOUT(pull_resistor_1_node),
    .WRITE(ttydriver_2_write), .DATA(ttydriver_2_data));
  TTY tty_3 (.data(ttydriver_3_data), .clk(CLK), .we(ttydriver_3_write));  // open: clr
  TTYDriver ttydriver_3 (
    .RXIN(pull_resistor_1_node), .CLK(CLK), .TTY_ADDR(in_5), .TXOUT(pull_resistor_1_node),
    .WRITE(ttydriver_3_write), .DATA(ttydriver_3_data));
  // Probe on vpwbmonitor_1_out_4
  // Probe on vpwbmonitor_1_last_fe
  // Probe on vpwbmonitor_1_last_addr
  // Probe on vpwbmonitor_1_last_data
endmodule

module KeyboardDriver (
  input  DR,
  input  [6:0] DATA,
  input  RXIN,
  input  [3:0] DEST,
  input  CLK,
  output TXOUT,
  output READ
);

  wire ADDR, and_1_out, CHKDR, CS, JUMP, O, or_1_out, txrxd_1_din, vpwbcontroller_1_ser_out, W;
  wire [5:5] rom_1_data;
  wire [7:0] NPC, PC, PCPLUS1, PCTARGET;
  wire [11:0] multiplexer_1_out;

  Register register_1 (.D(NPC), .en(1'b1), .clk(CLK), .Q(PC));  // open: clr
  Adder adder_1 (.a(8'h1), .b(PC), .out(PCPLUS1));  // open: cin, cout
  ROM #(.dataWidth(16)) rom_1 (.addr(PC), .data({PCTARGET, JUMP, CHKDR, rom_1_data[5], READ, ADDR, O, W, CS}));
  Multiplexer #(.width(12)) multiplexer_1 (.in0(12'h1), .in1({DEST, 1'b0, DATA}), .out(multiplexer_1_out), .sel(ADDR));
  VPWBController vpwbcontroller_1 (
    .O(O), .ADDR(ADDR), .DATAIN(multiplexer_1_out), .CS(CS), .W(W), .CLK(CLK), .SER_IN(txrxd_1_din),
    .SER_OUT(vpwbcontroller_1_ser_out));  // open: I, DATAOUT
  and and_1 (and_1_out, CHKDR, DR);
  or or_1 (or_1_out, and_1_out, JUMP);
  Multiplexer #(.width(8)) multiplexer_2 (.in0(PCPLUS1), .in1(PCTARGET), .out(NPC), .sel(or_1_out));
  TXRXD txrxd_1 (.DOUT(vpwbcontroller_1_ser_out), .RXIN(RXIN), .DIN(txrxd_1_din), .TXOUT(TXOUT));

  // Other names for the same wires on the sheet: DATA_t[6:0] = DATA

  // Notes on the sheet:
  //   contents of rom_1 (hex, n*v repeats v):
  //   7 4 7 547 387 1c 387
endmodule

module TTYDriver (
  input  RXIN,
  input  [3:0] TTY_ADDR,
  input  CLK,
  output [6:0] DATA,
  output TXOUT,
  output WRITE
);

  wire ADDR, and_1_out, CHKDR, comparator_1_eq, CS, DR, JUMP, not_1_out, O, or_1_out, txrxd_1_din,
       vpwbcontroller_1_ser_out, W, WRITE_TTY;
  wire [5:5] rom_1_data;
  wire [7:0] NPC, PC, PCPLUS1, PCTARGET;
  wire [11:0] DATAOUT, register_2_q;

  Register register_1 (.D(NPC), .en(1'b1), .clk(CLK), .Q(PC));  // open: clr
  Adder adder_1 (.a(8'h1), .b(PC), .out(PCPLUS1));  // open: cin, cout
  ROM #(.dataWidth(16)) rom_1 (.addr(PC), .data({PCTARGET, JUMP, CHKDR, rom_1_data[5], WRITE_TTY, ADDR, O, W, CS}));
  Register #(.width(12)) register_2 (
    .D(DATAOUT), .en(not_1_out), .clk(CLK), .Q({register_2_q[11:2], DR, register_2_q[0]}));  // open: clr
  not not_1 (not_1_out, O);
  and and_1 (and_1_out, CHKDR, DR);
  VPWBController vpwbcontroller_1 (
    .O(O), .ADDR(ADDR), .DATAIN({4'b1111, TTY_ADDR, 4'b0001}), .CS(CS), .W(W), .CLK(CLK),
    .SER_IN(txrxd_1_din), .DATAOUT(DATAOUT), .SER_OUT(vpwbcontroller_1_ser_out));  // open: I
  Multiplexer #(.width(8)) multiplexer_1 (.in0(PCPLUS1), .in1(PCTARGET), .out(NPC), .sel(or_1_out));
  or or_1 (or_1_out, and_1_out, JUMP);
  Comparator #(.mode("unsigned"), .width(4)) comparator_1 (
    .a(register_2_q[11:8]), .b(TTY_ADDR), .eq(comparator_1_eq));  // open: gt, lt
  and and_2 (WRITE, comparator_1_eq, WRITE_TTY);
  Multiplexer #(.width(7)) multiplexer_2 (
    .in0({7{1'b0}}), .in1({register_2_q[6:2], DR, register_2_q[0]}), .out(DATA), .sel(WRITE));
  TXRXD txrxd_1 (.DOUT(vpwbcontroller_1_ser_out), .RXIN(RXIN), .DIN(txrxd_1_din), .TXOUT(TXOUT));

  // Other names for the same wires on the sheet: CHAR[6:0] = DATA

  // Notes on the sheet:
  //   contents of rom_1 (hex, n*v repeats v):
  //   7 4 7 2 647 87 a 17 87
endmodule

module VPWBMonitor (
  input  RXIN,
  input  CLK,
  output [31:0] out_3,
  output [24:0] out_4,
  output LAST_FE,
  output [3:0] LAST_ADDR,
  output [7:0] LAST_DATA
);

  wire B0_ERR, B1_ERR, B2_ERR, B3_ERR, B4_ERR, B5_ERR, B6_ERR, B7_ERR, B8_ERR, B9_ERR, BA_ERR, BB_ERR,
       FOUND_IDLE, I4, I5, I6, I7, I8, I9, I10, I11, I12, I13, I14, I15, I16, I17, I18, I19, I20, I21, I22,
       I23, I24, I25, I26, I27, I28, I29, NEW_IDLE, not_7_out;
  wire [0:0] not_1_out, not_2_out, not_9_out, not_10_out, not_15_out, not_16_out, shifter_1_out_3,
       shifter_2_out_3, shifter_3_out_3, shifter_6_out_3, shifter_7_out_3, shifter_8_out_3, shifter_10_out_3,
       shifter_11_out_3, shifter_12_out_3;
  wire [1:0] shifter_1_out, shifter_2_out, shifter_3_out, shifter_6_out, shifter_7_out, shifter_8_out,
       shifter_10_out, shifter_11_out, shifter_12_out;
  wire [4:0] FRAME_LENGTH, priority_encoder_1_out;
  wire [5:0] subtractor_1_out, subtractor_2_out;
  wire [9:0] shifter_12_out_2;
  wire [10:0] shifter_11_out_2;
  wire [11:0] shifter_10_out_2, shifter_13_out;
  wire [13:0] shifter_8_out_2;
  wire [14:0] shifter_7_out_2;
  wire [15:0] shifter_6_out_2, shifter_9_out;
  wire [17:0] shifter_3_out_2;
  wire [18:0] shifter_2_out_2;
  wire [19:0] shifter_1_out_2, shifter_4_out;
  wire [24:0] and_6_out, not_8_out;
  wire [25:0] shifter_5_out;

  not not_1 (not_1_out[0], LAST_DATA[1]);
  not not_2 (not_2_out[0], LAST_DATA[3]);
  Subtractor #(.width(6)) subtractor_1 (
    .a(6'b011001), .b({1'b0, FRAME_LENGTH}), .out(subtractor_1_out));  // open: bin, bout
  Shifter #(.shift("lr"), .width(23)) shifter_1 (
    .in(out_4[24:2]), .\dist ({4'b0000, LAST_DATA[0]}),
    .out({shifter_1_out_2, shifter_1_out, shifter_1_out_3[0]}));
  Shifter #(.shift("lr"), .width(22)) shifter_2 (
    .in({shifter_1_out_2, shifter_1_out}), .\dist ({4'b0000, not_1_out[0]}),
    .out({shifter_2_out_2, shifter_2_out, shifter_2_out_3[0]}));
  Shifter #(.shift("lr"), .width(21)) shifter_3 (
    .in({shifter_2_out_2, shifter_2_out}), .\dist ({4'b0000, LAST_DATA[2]}),
    .out({shifter_3_out_2, shifter_3_out, shifter_3_out_3[0]}));
  Shifter #(.shift("lr"), .width(20)) shifter_4 (
    .in({shifter_3_out_2, shifter_3_out}), .\dist ({4'b0000, not_2_out[0]}), .out(shifter_4_out));
  // Probe on shifter_5_out
  and and_1 (B0_ERR, ~out_4[1], ~out_4[2], ~out_4[3]);  // AND_Gate
  not not_3 (LAST_DATA[0], out_4[2]);
  and and_2 (B1_ERR, shifter_1_out_3[0], shifter_1_out[0], shifter_1_out[1]);
  not not_4 (LAST_DATA[1], shifter_1_out[0]);
  and and_3 (B2_ERR, ~shifter_2_out_3[0], ~shifter_2_out[0], ~shifter_2_out[1]);  // AND_Gate
  not not_5 (LAST_DATA[2], shifter_2_out[0]);
  and and_4 (B3_ERR, shifter_3_out_3[0], shifter_3_out[0], shifter_3_out[1]);
  not not_6 (LAST_DATA[3], shifter_3_out[0]);
  not not_7 (not_7_out, RXIN);
  Shift_Register #(.length(32)) shift_register_1 (
    .shift(1'b1), .in(not_7_out), .clk(CLK), .out(out_3[31]), .q0(out_3[0]), .q1(out_3[1]), .q2(out_3[2]),
    .q3(out_3[3]), .q4(out_3[4]), .q5(out_3[5]), .q6(out_3[6]), .q7(out_3[7]), .q8(out_3[8]), .q9(out_3[9]),
    .q10(out_3[10]), .q11(out_3[11]), .q12(out_3[12]), .q13(out_3[13]), .q14(out_3[14]), .q15(out_3[15]),
    .q16(out_3[16]), .q17(out_3[17]), .q18(out_3[18]), .q19(out_3[19]), .q20(out_3[20]), .q21(out_3[21]),
    .q22(out_3[22]), .q23(out_3[23]), .q24(out_3[24]), .q25(out_3[25]), .q26(out_3[26]), .q27(out_3[27]),
    .q28(out_3[28]), .q29(out_3[29]), .q30(out_3[30]));  // open: load, clr, d0, d1, d2, d3, d4, d5, d6, d7, d8, d9, d10, d11, d12, d13, d14, d15, d16, d17, d18, d19, d20, d21, d22, d23, d24, d25, d26, d27, d28, d29, d30, d31, q31
  and and_5 (NEW_IDLE, ~out_3[0], ~out_3[1], ~out_3[2], out_3[3]);  // AND_Gate
  assign not_8_out = ~shifter_5_out[24:0];  // NOT_Gate not_8, 25 bits wide
  Shifter #(.shift("ar"), .width(26)) shifter_5 (.in(26'h2000000), .\dist (subtractor_1_out[4:0]), .out(shifter_5_out));
  not not_9 (not_9_out[0], LAST_DATA[5]);
  not not_10 (not_10_out[0], LAST_DATA[7]);
  Shifter #(.shift("lr"), .width(19)) shifter_6 (
    .in(shifter_4_out[19:1]), .\dist ({4'b0000, LAST_DATA[4]}),
    .out({shifter_6_out_2, shifter_6_out, shifter_6_out_3[0]}));
  Shifter #(.shift("lr"), .width(18)) shifter_7 (
    .in({shifter_6_out_2, shifter_6_out}), .\dist ({4'b0000, not_9_out[0]}),
    .out({shifter_7_out_2, shifter_7_out, shifter_7_out_3[0]}));
  Shifter #(.shift("lr"), .width(17)) shifter_8 (
    .in({shifter_7_out_2, shifter_7_out}), .\dist ({4'b0000, LAST_DATA[6]}),
    .out({shifter_8_out_2, shifter_8_out, shifter_8_out_3[0]}));
  Shifter #(.shift("lr"), .width(16)) shifter_9 (
    .in({shifter_8_out_2, shifter_8_out}), .\dist ({3'b000, not_10_out[0]}), .out(shifter_9_out));
  // Probe on and_6_out
  Register #(.width(25)) register_1 (.D(and_6_out), .en(NEW_IDLE), .clk(CLK), .Q(out_4));  // open: clr
  assign and_6_out = out_3[27:3] & not_8_out;  // AND_Gate and_6, 25 bits wide
  and and_7 (B4_ERR, ~shifter_4_out[0], ~shifter_4_out[1], ~shifter_4_out[2]);  // AND_Gate
  not not_11 (LAST_DATA[4], shifter_4_out[1]);
  and and_8 (B5_ERR, shifter_6_out_3[0], shifter_6_out[0], shifter_6_out[1]);
  not not_12 (LAST_DATA[5], shifter_6_out[0]);
  and and_9 (B6_ERR, ~shifter_7_out_3[0], ~shifter_7_out[0], ~shifter_7_out[1]);  // AND_Gate
  not not_13 (LAST_DATA[6], shifter_7_out[0]);
  and and_10 (B7_ERR, shifter_8_out_3[0], shifter_8_out[0], shifter_8_out[1]);
  not not_14 (LAST_DATA[7], shifter_8_out[0]);
  not not_15 (not_15_out[0], LAST_ADDR[1]);
  not not_16 (not_16_out[0], LAST_ADDR[3]);
  and and_11 (B8_ERR, ~shifter_9_out[0], ~shifter_9_out[1], ~shifter_9_out[2]);  // AND_Gate
  not not_17 (LAST_ADDR[0], shifter_9_out[1]);
  Shifter #(.shift("lr"), .width(15)) shifter_10 (
    .in(shifter_9_out[15:1]), .\dist ({3'b000, LAST_ADDR[0]}),
    .out({shifter_10_out_2, shifter_10_out, shifter_10_out_3[0]}));
  and and_12 (B9_ERR, shifter_10_out_3[0], shifter_10_out[0], shifter_10_out[1]);
  not not_18 (LAST_ADDR[1], shifter_10_out[0]);
  Shifter #(.shift("lr"), .width(14)) shifter_11 (
    .in({shifter_10_out_2, shifter_10_out}), .\dist ({3'b000, not_15_out[0]}),
    .out({shifter_11_out_2, shifter_11_out, shifter_11_out_3[0]}));
  and and_13 (BA_ERR, ~shifter_11_out_3[0], ~shifter_11_out[0], ~shifter_11_out[1]);  // AND_Gate
  not not_19 (LAST_ADDR[2], shifter_11_out[0]);
  Shifter #(.shift("lr"), .width(13)) shifter_12 (
    .in({shifter_11_out_2, shifter_11_out}), .\dist ({3'b000, LAST_ADDR[2]}),
    .out({shifter_12_out_2, shifter_12_out, shifter_12_out_3[0]}));
  and and_14 (BB_ERR, shifter_12_out_3[0], shifter_12_out[0], shifter_12_out[1]);
  not not_20 (LAST_ADDR[3], shifter_12_out[0]);
  Shifter #(.shift("lr"), .width(12)) shifter_13 (
    .in({shifter_12_out_2, shifter_12_out}), .\dist ({3'b000, not_16_out[0]}), .out(shifter_13_out));
  and and_15 (I29, ~out_3[31], ~out_3[30], ~out_3[29]);  // AND_Gate
  and and_16 (I28, ~out_3[30], ~out_3[29], ~out_3[28]);  // AND_Gate
  and and_17 (I27, ~out_3[29], ~out_3[28], ~out_3[27]);  // AND_Gate
  and and_18 (I26, ~out_3[28], ~out_3[27], ~out_3[26]);  // AND_Gate
  and and_19 (I24, ~out_3[26], ~out_3[25], ~out_3[24]);  // AND_Gate
  and and_20 (I23, ~out_3[25], ~out_3[24], ~out_3[23]);  // AND_Gate
  and and_21 (I25, ~out_3[27], ~out_3[26], ~out_3[25]);  // AND_Gate
  or or_1 (LAST_FE, out_4[1], B0_ERR, B1_ERR, B2_ERR, B3_ERR, B4_ERR, B5_ERR, B6_ERR, B7_ERR, B8_ERR, B9_ERR, BA_ERR, BB_ERR);
  and and_22 (I22, ~out_3[24], ~out_3[23], ~out_3[22]);  // AND_Gate
  and and_23 (I21, ~out_3[23], ~out_3[22], ~out_3[21]);  // AND_Gate
  and and_24 (I20, ~out_3[22], ~out_3[21], ~out_3[20]);  // AND_Gate
  and and_25 (I19, ~out_3[21], ~out_3[20], ~out_3[19]);  // AND_Gate
  and and_26 (I18, ~out_3[20], ~out_3[19], ~out_3[18]);  // AND_Gate
  and and_27 (I17, ~out_3[19], ~out_3[18], ~out_3[17]);  // AND_Gate
  and and_28 (I16, ~out_3[18], ~out_3[17], ~out_3[16]);  // AND_Gate
  and and_29 (I15, ~out_3[17], ~out_3[16], ~out_3[15]);  // AND_Gate
  and and_30 (I14, ~out_3[16], ~out_3[15], ~out_3[14]);  // AND_Gate
  and and_31 (I13, ~out_3[15], ~out_3[14], ~out_3[13]);  // AND_Gate
  and and_32 (I12, ~out_3[14], ~out_3[13], ~out_3[12]);  // AND_Gate
  and and_33 (I11, ~out_3[13], ~out_3[12], ~out_3[11]);  // AND_Gate
  and and_34 (I10, ~out_3[12], ~out_3[11], ~out_3[10]);  // AND_Gate
  and and_35 (I9, ~out_3[11], ~out_3[10], ~out_3[9]);  // AND_Gate
  and and_36 (I8, ~out_3[10], ~out_3[9], ~out_3[8]);  // AND_Gate
  and and_37 (I7, ~out_3[9], ~out_3[8], ~out_3[7]);  // AND_Gate
  and and_38 (I6, ~out_3[8], ~out_3[7], ~out_3[6]);  // AND_Gate
  and and_39 (I5, ~out_3[7], ~out_3[6], ~out_3[5]);  // AND_Gate
  and and_40 (I4, ~out_3[6], ~out_3[5], ~out_3[4]);  // AND_Gate
  Priority_Encoder #(.select(5)) priority_encoder_1 (
    .in0(I29), .in1(I28), .in2(I27), .in3(I26), .in4(I25), .in5(I24), .in6(I23), .in7(I22), .in8(I21),
    .in9(I20), .in10(I19), .in11(I18), .in12(I17), .in13(I16), .in14(I15), .in15(I14), .in16(I13),
    .in17(I12), .in18(I11), .in19(I10), .in20(I9), .in21(I8), .in22(I7), .in23(I6), .in24(I5), .in25(I4),
    .in26(1'b0), .in27(1'b0), .in28(1'b0), .in29(1'b0), .in30(1'b0), .in31(1'b0),
    .out(priority_encoder_1_out), .gs(FOUND_IDLE));  // open: en_out, en_in
  Subtractor #(.width(6)) subtractor_2 (
    .a(6'b011010), .b({1'b0, priority_encoder_1_out}), .out(subtractor_2_out));  // open: bin, bout
  Multiplexer #(.width(5)) multiplexer_1 (
    .in0({5{1'b0}}), .in1(subtractor_2_out[4:0]), .out(FRAME_LENGTH), .sel(FOUND_IDLE));

  // Other names for the same wires on the sheet: LAST_FRAME[24:0] = out_4; HIST[31:0] = out_3; B8 = LAST_ADDR[0];
  //   B9 = LAST_ADDR[1]; BA = LAST_ADDR[2]; BB = LAST_ADDR[3]; B0 = LAST_DATA[0]; B1 = LAST_DATA[1];
  //   B2 = LAST_DATA[2]; B3 = LAST_DATA[3]; B4 = LAST_DATA[4]; B5 = LAST_DATA[5]; B6 = LAST_DATA[6];
  //   B7 = LAST_DATA[7]; EOF_ERR = out_4[1]
endmodule

module TXRXD (
  input  DOUT,
  input  RXIN,
  output TXOUT,
  output DIN
);

  assign TXOUT = DOUT ? ~DOUT : 1'bz;  // Controlled_Inverter controlled_inverter_1
  not not_1 (DIN, RXIN);

  // Notes on the sheet:
  //   TXOUT: pull=down
endmodule

module VPWBController (
  input  CS,
  input  W,
  input  SER_IN,
  input  O,
  input  ADDR,
  input  [11:0] DATAIN,
  input  CLK,
  output SER_OUT,
  output I,
  output [11:0] DATAOUT
);

  wire DR, EMPTY, ENA, not_1_out, READ, RXFULL, TBNF, TXFULL, TXI, TXIDLE, WRITE;
  wire [11:1] register_1_q;

  and and_1 (WRITE, W, CS, ADDR);
  and and_2 (READ, O, CS, ADDR);
  VPWBRX vpwbrx_1 (
    .READ(READ), .ENA(ENA), .CLK(CLK), .SER_IN(SER_IN), .FRAME_OUT(DATAOUT), .FULL(RXFULL), .EMPTY(EMPTY));  // open: CARE, ADDR, out_11, out_10
  Register #(.width(12)) register_1 (.D(DATAIN), .en(not_1_out), .clk(CLK), .Q({register_1_q, ENA}));  // open: clr
  not not_1 (not_1_out, ADDR);
  VPWBTX vpwbtx_1 (
    .FRAME_IN(DATAIN), .WRITE(WRITE), .ENA(ENA), .CLK(CLK), .SER_IN(SER_IN), .FULL(TXFULL), .IDLE(TXIDLE),
    .SER_OUT(SER_OUT));
  and and_3 (DR, register_1_q[1], ~EMPTY);  // AND_Gate
  and and_4 (TXI, register_1_q[3], TXIDLE);
  and and_5 (TBNF, TXFULL, register_1_q[2]);
endmodule

module VPWBTX (
  input  [11:0] FRAME_IN,
  input  SER_IN,
  input  WRITE,
  input  ENA,
  input  CLK,
  output SER_OUT,
  output FULL,
  output IDLE
);

  wire and_1_out, ARBL, BITCMP, BUSIDLE, DEQUEU, DIN, EMPTY, NEWBIT, Nottransmit, or_1_out, SHIFT_DW,
       SRO_EMPTY, SRO_OUT, Transmitting;
  wire [3:0] BL;
  wire [11:0] FRAME_OUT;

  and and_1 (and_1_out, ~ARBL, ~SRO_EMPTY);  // AND_Gate
  and and_2 (Nottransmit, BUSIDLE, ~SRO_EMPTY, ~Transmitting);  // AND_Gate
  or or_1 (or_1_out, Nottransmit, and_1_out);
  VPWBObserver vpwbobserver_1 (.ENA(ENA), .CLK(CLK), .RX(SER_IN), .DIN(DIN), .NEWBIT(NEWBIT), .IDLE(BUSIDLE));
  VPWBSRO vpwbsro_1 (
    .LOAD(DEQUEU), .ENA(ENA), .PARA_IN(FRAME_OUT), .CLK(CLK), .SHIFT(SHIFT_DW), .RELOAD(ARBL),
    .EMPTY(SRO_EMPTY), .SER_OUT(SRO_OUT), .BITSLEFT(BL));
  D_Flip_Flop d_ff_1 (.D(or_1_out), .clk(CLK), .Q(Transmitting));  // open: Qn, preset, reset
  VPWBArbiter vpwbarbiter_1 (
    .DW(SHIFT_DW), .EVENBIT(BL[0]), .DOUT(SRO_OUT), .ENA(ENA), .CLK(CLK), .RX(SER_IN), .ARBL(ARBL),
    .BITCMP(BITCMP), .TX(SER_OUT));
  VPWBFrameQueue vpwbframequeue_1 (
    .FRAME_IN(FRAME_IN), .ENQUEUE(WRITE), .ENA(ENA), .CLK(CLK), .DEQUEUE(DEQUEU), .FULL(FULL),
    .FRAME_OUT(FRAME_OUT), .EMPTY(EMPTY));
  and and_3 (IDLE, EMPTY, SRO_EMPTY);
  and and_4 (DEQUEU, ~EMPTY, SRO_EMPTY);  // AND_Gate
  and and_5 (SHIFT_DW, BITCMP, ~SRO_EMPTY, Transmitting);  // AND_Gate

  // Other names for the same wires on the sheet: EVNBIT = BL[0]

  // Notes on the sheet:
  //   queue EMPTY and transmitter IDLE
  //   observer NOTIDLE is 
  //   whatever goes into DW should go into IDLE
endmodule

module VPWBRX (
  input  [3:0] CARE,
  input  [3:0] ADDR,
  input  SER_IN,
  input  READ,
  input  ENA,
  input  CLK,
  output [11:0] FRAME_OUT,
  output FULL,
  output EMPTY,
  output out_10,
  output [11:0] out_11
);

  wire and_1_out, ENQUEUE, FULL_FRAME, IS_IDLE, Newbit;

  VPWBObserver vpwbobserver_1 (.ENA(ENA), .CLK(CLK), .RX(SER_IN), .DIN(out_10), .NEWBIT(Newbit), .IDLE(IS_IDLE));
  and and_1 (and_1_out, FULL_FRAME, ~FULL);  // AND_Gate
  VPWBSRI vpwbsri_1 (
    .READ(and_1_out), .ENA(ENA), .CLK(CLK), .SER_IN(out_10), .NEWBIT(Newbit), .CLEAR(IS_IDLE),
    .FULL(FULL_FRAME), .PARA_OUT(out_11));
  and and_2 (ENQUEUE, FULL_FRAME, ~FULL);  // AND_Gate
  VPWBFrameQueue vpwbframequeue_1 (
    .FRAME_IN(out_11), .ENQUEUE(ENQUEUE), .ENA(ENA), .CLK(CLK), .DEQUEUE(READ), .FULL(FULL),
    .FRAME_OUT(FRAME_OUT), .EMPTY(EMPTY));

  // Other names for the same wires on the sheet: PARA_OUT[11:0] = out_11; SRI_INPUT = out_10
endmodule

module VPWBFrameQueue (
  input  [11:0] FRAME_IN,
  input  ENQUEUE,
  input  DEQUEUE,
  input  ENA,
  input  CLK,
  output [11:0] FRAME_OUT,
  output FULL,
  output EMPTY
);

  wire and_1_out, and_2_out, DEQUEUE_CT0, DEQUEUE_CT1, DEQUEUE_CT2, DEQUEUE_CT3, ENQUEUE_CT0, ENQUEUE_CT1,
       ENQUEUE_CT2, ENQUEUE_CT3, FULL_EMPTY_COUNTER, not_1_out, not_2_out, not_3_out, not_4_out, not_5_out,
       not_6_out, not_7_out, not_8_out, not_9_out, not_10_out;
  wire [1:0] DEQUEUE_COUNTER, ENQUEUE_COUNTER;
  wire [2:0] ACTUAL_COUNT;
  wire [11:0] FIRST_FRAME, FOURTH_FRAME, FRAME_SELECTED, SECOND_FRAME, THIRD_FRAME;

  Demultiplexer #(.select(2)) demultiplexer_1 (
    .out0(ENQUEUE_CT0), .out1(ENQUEUE_CT1), .out2(ENQUEUE_CT2), .out3(ENQUEUE_CT3), .in(1'b1),
    .sel(ENQUEUE_COUNTER));
  Demultiplexer #(.select(2)) demultiplexer_2 (
    .out0(DEQUEUE_CT0), .out1(DEQUEUE_CT1), .out2(DEQUEUE_CT2), .out3(DEQUEUE_CT3), .in(1'b1),
    .sel(DEQUEUE_COUNTER));
  not not_1 (not_1_out, DEQUEUE);
  not not_2 (not_2_out, ENQUEUE);
  and and_1 (and_1_out, ENQUEUE, not_1_out);
  and and_2 (and_2_out, DEQUEUE, not_2_out);
  Register #(.width(12)) register_1 (.D(FRAME_IN), .en(ENQUEUE_CT0), .clk(CLK), .Q(FIRST_FRAME), .clr(not_3_out));
  not not_3 (not_3_out, ENA);
  Multiplexer #(.select(2), .width(12)) multiplexer_1 (
    .in0(FIRST_FRAME), .in1(SECOND_FRAME), .in2(THIRD_FRAME), .in3(FOURTH_FRAME), .out(FRAME_SELECTED),
    .sel(DEQUEUE_COUNTER));
  or or_1 (FULL_EMPTY_COUNTER, and_1_out, and_2_out);
  not not_4 (not_4_out, ENA);
  Counter #(.max('h3), .width(2)) counter_1 (
    .count(ENQUEUE), .Q(ENQUEUE_COUNTER), .clk(CLK));  // open: load, D, carry, up, clr
  Counter #(.max('h3), .width(2)) counter_2 (
    .count(DEQUEUE), .Q(DEQUEUE_COUNTER), .clk(CLK));  // open: load, D, carry, up, clr
  Register #(.width(12)) register_2 (.D(FRAME_IN), .en(ENQUEUE_CT1), .clk(CLK), .Q(SECOND_FRAME), .clr(not_4_out));
  Register #(.width(12)) register_3 (.D(FRAME_SELECTED), .en(DEQUEUE), .clk(CLK), .Q(FRAME_OUT));  // open: clr
  Register #(.width(12)) register_4 (.D(FRAME_IN), .en(ENQUEUE_CT2), .clk(CLK), .Q(THIRD_FRAME), .clr(not_5_out));
  not not_5 (not_5_out, ENA);
  Counter #(.max('h4), .width(3)) counter_3 (
    .count(FULL_EMPTY_COUNTER), .Q(ACTUAL_COUNT), .up(ENQUEUE), .clk(CLK));  // open: load, D, carry, clr
  not not_6 (not_6_out, ENA);
  Register #(.width(12)) register_5 (.D(FRAME_IN), .en(ENQUEUE_CT3), .clk(CLK), .Q(FOURTH_FRAME), .clr(not_6_out));
  not not_7 (not_7_out, ACTUAL_COUNT[0]);
  not not_8 (not_8_out, ACTUAL_COUNT[1]);
  not not_9 (not_9_out, ACTUAL_COUNT[2]);
  not not_10 (not_10_out, ACTUAL_COUNT[2]);
  and and_3 (EMPTY, not_7_out, not_8_out, not_9_out);
  and and_4 (FULL, ACTUAL_COUNT[0], ACTUAL_COUNT[1], not_10_out);

  // Notes on the sheet:
  //   MSB leaves out first
  //   LSB of bits left as EVENBIT when connecting arbiter to SRI/O
  //   COUNTER GO UP WHEN ENQUEUE, COUNTER DOWN WHEN DEQUEUE, NOTHING WHEN ENQUEUE AND DEQUEUEU
endmodule

module VPWBSRI (
  input  READ,
  input  SER_IN,
  input  NEWBIT,
  input  CLEAR,
  input  ENA,
  input  CLK,
  output FULL,
  output [11:0] PARA_OUT
);

  wire FULLCOUNT, not_1_out, not_2_out, not_3_out, or_1_out, WE;
  wire [3:0] counter_1_q;
  wire [11:0] shift_register_1_q0;

  and and_1 (WE, SER_IN, FULLCOUNT);
  Shift_Register #(.length(12)) shift_register_1 (
    .shift(NEWBIT), .in(SER_IN), .clk(CLK), .out(shift_register_1_q0[11]), .q0(shift_register_1_q0[0]),
    .q1(shift_register_1_q0[1]), .q2(shift_register_1_q0[2]), .q3(shift_register_1_q0[3]),
    .q4(shift_register_1_q0[4]), .q5(shift_register_1_q0[5]), .q6(shift_register_1_q0[6]),
    .q7(shift_register_1_q0[7]), .q8(shift_register_1_q0[8]), .q9(shift_register_1_q0[9]),
    .q10(shift_register_1_q0[10]));  // open: load, clr, d0, d1, d2, d3, d4, d5, d6, d7, d8, d9, d10, d11, q11
  Register #(.width(12)) register_1 (.D(shift_register_1_q0), .en(WE), .clk(CLK), .Q(PARA_OUT), .clr(not_1_out));
  not not_1 (not_1_out, ENA);
  not not_2 (not_2_out, ENA);
  Register #(.width(1)) register_2 (.D(WE), .en(or_1_out), .clk(CLK), .Q(FULL), .clr(not_3_out));
  or or_1 (or_1_out, READ, WE);
  not not_3 (not_3_out, ENA);
  Counter #(.max('hd), .width(4)) counter_1 (
    .load(CLEAR), .D(4'b0000), .count(NEWBIT), .Q(counter_1_q), .clk(CLK), .clr(not_2_out));  // open: carry, up
  Comparator #(.width(4)) comparator_1 (.a(counter_1_q), .b(4'b1100), .eq(FULLCOUNT));  // open: gt, lt
endmodule

module VPWBSRO (
  input  [11:0] PARA_IN,
  input  LOAD,
  input  SHIFT,
  input  RELOAD,
  input  ENA,
  input  CLK,
  output SER_OUT,
  output EMPTY,
  output [3:0] BITSLEFT
);

  wire and_1_out, and_2_out, not_1_out, reOL;
  wire [3:0] counter_1_q;
  wire [11:0] multiplexer_1_out, register_1_q;

  and and_1 (and_1_out, SHIFT, ~LOAD);  // AND_Gate
  Shift_Register #(.length(13)) shift_register_1 (
    .shift(and_1_out), .in(1'b0), .clk(CLK), .out(SER_OUT), .load(reOL), .d0(1'b1),
    .d1(multiplexer_1_out[0]), .d2(multiplexer_1_out[1]), .d3(multiplexer_1_out[2]),
    .d4(multiplexer_1_out[3]), .d5(multiplexer_1_out[4]), .d6(multiplexer_1_out[5]),
    .d7(multiplexer_1_out[6]), .d8(multiplexer_1_out[7]), .d9(multiplexer_1_out[8]),
    .d10(multiplexer_1_out[9]), .d11(multiplexer_1_out[10]), .d12(multiplexer_1_out[11]));  // open: clr, q0, q1, q2, q3, q4, q5, q6, q7, q8, q9, q10, q11, q12
  Multiplexer #(.width(12)) multiplexer_1 (.in0(PARA_IN), .in1(register_1_q), .out(multiplexer_1_out), .sel(RELOAD));
  Register #(.width(12)) register_1 (.D(PARA_IN), .en(LOAD), .clk(CLK), .Q(register_1_q));  // open: clr
  and and_2 (and_2_out, SHIFT, ~EMPTY);  // AND_Gate
  Counter #(.max('hd), .width(4)) counter_1 (
    .load(reOL), .D(4'b1101), .count(and_2_out), .Q(counter_1_q), .up(1'b0), .clk(CLK), .clr(not_1_out));  // open: carry
  not not_1 (not_1_out, ENA);
  Subtractor #(.width(4)) subtractor_1 (.a(counter_1_q), .b(4'b0000), .out(BITSLEFT));  // open: bin, bout
  Comparator #(.width(4)) comparator_1 (.a(counter_1_q), .b(4'b0000), .eq(EMPTY));  // open: gt, lt
  or or_1 (reOL, LOAD, RELOAD);
endmodule

module VPWBArbiter (
  input  EVENBIT,
  input  DOUT,
  input  DW,
  input  RX,
  input  ENA,
  input  CLK,
  output TX,
  output ARBL,
  output BITCMP
);

  wire ACTUAL_EVENBIT, and_1_out, and_2_out, and_3_out, and_4_out, and_5_out, and_6_out, and_10_out,
       BIT1STAGE, BIT2STAGE, ENTER_ARBL, ENTER_BIT1, ENTER_BIT2, ENTER_IDLE, IDLESTAGE, LONG_CYCLE,
       LONG_CYCLE_SNAP, not_1_out, not_2_out, not_3_out, not_4_out, not_5_out, not_8_out, not_9_out,
       not_10_out, not_11_out, or_1_out, R, SHORT_CYCLE, xor_1_out;

  not not_1 (not_1_out, LONG_CYCLE);
  not not_2 (not_2_out, DW);
  not not_3 (not_3_out, DW);
  not not_4 (not_4_out, DW);
  not not_5 (not_5_out, LONG_CYCLE);
  Register #(.width(1)) register_1 (.D(EVENBIT), .en(ENTER_BIT1), .clk(CLK), .Q(ACTUAL_EVENBIT));  // open: clr
  not not_6 (R, ENA);
  and and_1 (and_1_out, IDLESTAGE, not_2_out);
  and and_2 (and_2_out, BIT1STAGE, not_1_out, not_3_out);
  and and_3 (and_3_out, BIT2STAGE, not_4_out);
  and and_4 (and_4_out, IDLESTAGE, DW);
  and and_5 (and_5_out, BIT1STAGE, not_5_out, DW);
  and and_6 (and_6_out, BIT2STAGE, DW);
  and and_7 (ENTER_BIT2, LONG_CYCLE, BIT1STAGE);
  or or_1 (or_1_out, and_1_out, and_2_out, and_3_out);
  or or_2 (ENTER_BIT1, and_4_out, and_5_out, and_6_out);
  or or_3 (ENTER_IDLE, ARBL, or_1_out);
  Register #(.width(1)) register_2 (.D(LONG_CYCLE_SNAP), .en(ENTER_BIT1), .clk(CLK), .Q(LONG_CYCLE));  // open: clr
  not not_7 (SHORT_CYCLE, LONG_CYCLE_SNAP);
  not not_8 (not_8_out, IDLESTAGE);
  xor xor_1 (xor_1_out, TX, RX);
  xor xor_2 (LONG_CYCLE_SNAP, EVENBIT, DOUT);
  and and_8 (ENTER_ARBL, not_8_out, xor_1_out);
  D_Flip_Flop d_ff_1 (.D(not_9_out), .clk(CLK), .Qn(IDLESTAGE), .reset(R));  // open: Q, preset
  not not_9 (not_9_out, ENTER_IDLE);
  T_Flip_Flop t_ff_1 (.T(ENTER_ARBL), .clk(CLK), .Q(ARBL));  // open: Qn, reset, preset
  D_Flip_Flop d_ff_2 (.D(ENTER_BIT1), .clk(CLK), .Q(BIT1STAGE), .reset(R));  // open: Qn, preset
  not not_10 (not_10_out, IDLESTAGE);
  not not_11 (not_11_out, LONG_CYCLE);
  and and_9 (TX, ACTUAL_EVENBIT, not_10_out);
  and and_10 (and_10_out, BIT1STAGE, not_11_out);
  D_Flip_Flop d_ff_3 (.D(ENTER_BIT2), .clk(CLK), .Q(BIT2STAGE), .reset(R));  // open: Qn, preset
  or or_4 (BITCMP, IDLESTAGE, and_10_out, BIT2STAGE);
endmodule

module VPWBObserver (
  input  RX,
  input  ENA,
  input  CLK,
  output IDLE,
  output DIN,
  output NEWBIT
);

  wire and_1_out, and_2_out, and_3_out, and_4_out, and_5_out, and_8_out, and_9_out, and_10_out, and_11_out,
       and_12_out, and_13_out, and_14_out, and_15_out, and_16_out, and_17_out, and_18_out, and_19_out,
       and_20_out, and_21_out, and_22_out, and_23_out, and_24_out, and_25_out, and_26_out, and_27_out,
       and_29_out, and_30_out, and_31_out, and_32_out, and_33_out, and_34_out, and_35_out, and_36_out,
       and_37_out, and_38_out, and_39_out, and_40_out, CLK_WRITE, DIN1, DIN2, DIN3, DIN4, INP, not_1_out,
       not_2_out, not_3_out, not_4_out, not_5_out, not_6_out, not_7_out, not_8_out, not_9_out, not_10_out,
       not_11_out, not_12_out, not_13_out, not_14_out, not_15_out, not_16_out, not_17_out, not_18_out,
       not_19_out, not_20_out, not_21_out, not_22_out, not_23_out, not_24_out, not_25_out, not_26_out,
       not_27_out, not_28_out, not_29_out, not_30_out, not_31_out, not_32_out, not_33_out, not_34_out,
       not_35_out, not_36_out, not_37_out, not_38_out, not_39_out, not_40_out, not_41_out, not_42_out,
       not_43_out, not_44_out, not_45_out, not_46_out, or_3_out, Q0, Q0_NEXT, Q1, Q1_NEXT, Q2, Q2_NEXT;
  wire [1:0] d_ff_6_q;

  not not_1 (not_1_out, Q0);
  not not_2 (not_2_out, Q1);
  not not_3 (not_3_out, Q0);
  not not_4 (not_4_out, Q2);
  not not_5 (not_5_out, INP);
  and and_1 (and_1_out, Q2, Q1, not_1_out);
  and and_2 (and_2_out, Q2, Q0, not_2_out);
  and and_3 (and_3_out, not_3_out, Q1, INP);
  and and_4 (and_4_out, INP, Q1, Q2);
  and and_5 (and_5_out, Q1, Q0, not_4_out, not_5_out);
  or or_1 (Q2_NEXT, and_2_out, and_3_out, and_1_out, and_4_out, and_5_out);
  and and_6 (CLK_WRITE, ENA, CLK);
  and and_7 (INP, ENA, RX);
  D_Flip_Flop d_ff_1 (.D(Q2_NEXT), .clk(CLK_WRITE), .Q(Q2));  // open: Qn, preset, reset
  not not_6 (not_6_out, Q2_NEXT);
  not not_7 (not_7_out, Q2);
  not not_8 (not_8_out, Q2_NEXT);
  not not_9 (not_9_out, Q1_NEXT);
  not not_10 (not_10_out, Q1);
  not not_11 (not_11_out, Q0);
  not not_12 (not_12_out, Q2_NEXT);
  not not_13 (not_13_out, Q1_NEXT);
  not not_14 (not_14_out, INP);
  and and_8 (and_8_out, not_14_out, Q1, not_15_out);
  not not_15 (not_15_out, Q0);
  not not_16 (not_16_out, Q1);
  and and_9 (and_9_out, not_16_out, Q0, not_17_out);
  not not_17 (not_17_out, Q2);
  and and_10 (and_10_out, Q0, not_18_out, not_19_out);
  not not_18 (not_18_out, Q1);
  not not_19 (not_19_out, INP);
  not not_20 (not_20_out, Q2);
  not not_21 (not_21_out, Q1);
  and and_11 (and_11_out, not_20_out, not_21_out, Q0);
  not not_22 (not_22_out, Q2_NEXT);
  and and_12 (and_12_out, not_22_out, Q1_NEXT, Q0_NEXT);
  not not_23 (not_23_out, Q2);
  and and_13 (and_13_out, not_23_out, Q1, not_24_out);
  not not_24 (not_24_out, Q0);
  and and_14 (and_14_out, not_6_out, Q1_NEXT, Q0_NEXT);
  and and_15 (and_15_out, not_7_out, Q1, Q0);
  and and_16 (and_16_out, not_8_out, not_9_out, Q0_NEXT);
  and and_17 (and_17_out, Q2, not_10_out, not_11_out);
  and and_18 (and_18_out, not_12_out, not_13_out, Q0_NEXT);
  D_Flip_Flop d_ff_2 (.D(Q1_NEXT), .clk(CLK_WRITE), .Q(Q1));  // open: Qn, preset, reset
  and and_19 (and_19_out, and_11_out, and_12_out);
  and and_20 (and_20_out, and_13_out, and_14_out);
  and and_21 (and_21_out, and_15_out, and_16_out);
  and and_22 (and_22_out, and_17_out, and_18_out);
  or or_2 (Q1_NEXT, and_8_out, and_9_out, and_10_out);
  D_Flip_Flop d_ff_3 (.D(Q0_NEXT), .clk(CLK_WRITE), .Q(Q0));  // open: Qn, preset, reset
  not not_25 (not_25_out, Q0);
  not not_26 (not_26_out, Q0);
  not not_27 (not_27_out, Q1);
  not not_28 (not_28_out, Q2);
  not not_29 (not_29_out, INP);
  not not_30 (not_30_out, Q2);
  not not_31 (not_31_out, Q1);
  not not_32 (not_32_out, Q0);
  and and_23 (and_23_out, Q1, not_25_out);
  and and_24 (and_24_out, not_26_out, INP);
  and and_25 (and_25_out, INP, Q2);
  and and_26 (and_26_out, Q1, INP);
  and and_27 (and_27_out, not_27_out, Q0, not_28_out, not_29_out);
  or or_3 (or_3_out, and_19_out, and_20_out, and_21_out, and_22_out);
  and and_28 (IDLE, not_30_out, not_31_out, not_32_out);
  or or_4 (Q0_NEXT, and_23_out, and_24_out, and_25_out, and_26_out, and_27_out);
  D_Flip_Flop d_ff_4 (.D(or_3_out), .clk(CLK), .Q(NEWBIT), .reset(not_33_out));  // open: Qn, preset
  not not_33 (not_33_out, ENA);
  D_Flip_Flop d_ff_5 (.D(Q1), .clk(CLK), .Q(d_ff_6_q[1]));  // open: Qn, preset, reset
  D_Flip_Flop d_ff_6 (.D(Q0), .clk(CLK), .Q(d_ff_6_q[0]));  // open: Qn, preset, reset
  not not_34 (not_34_out, Q2);
  not not_35 (not_35_out, Q1);
  not not_36 (not_36_out, Q2_NEXT);
  not not_37 (not_37_out, Q2);
  not not_38 (not_38_out, Q2_NEXT);
  not not_39 (not_39_out, Q1_NEXT);
  Multiplexer #(.select(2)) multiplexer_1 (.in0(DIN1), .in1(DIN2), .in2(DIN3), .in3(DIN4), .out(DIN), .sel(d_ff_6_q));
  and and_29 (and_29_out, not_34_out, not_35_out, Q0);
  and and_30 (and_30_out, not_36_out, Q1_NEXT, Q0_NEXT);
  not not_40 (not_40_out, Q2);
  and and_31 (and_31_out, not_40_out, Q1, not_41_out);
  not not_41 (not_41_out, Q0);
  not not_42 (not_42_out, Q2_NEXT);
  and and_32 (and_32_out, not_42_out, Q1_NEXT, Q0_NEXT);
  and and_33 (and_33_out, not_37_out, Q1, Q0);
  and and_34 (and_34_out, not_38_out, not_39_out, Q0_NEXT);
  and and_35 (and_35_out, and_29_out, and_30_out);
  and and_36 (and_36_out, and_31_out, and_32_out);
  and and_37 (and_37_out, and_33_out, and_34_out);
  Register #(.width(1)) register_1 (.D(1'b1), .en(and_35_out), .clk(CLK), .Q(DIN2));  // open: clr
  Register #(.width(1)) register_2 (.D(1'b0), .en(and_36_out), .clk(CLK), .Q(DIN3));  // open: clr
  Register #(.width(1)) register_3 (.D(1'b0), .en(and_37_out), .clk(CLK), .Q(DIN4));  // open: clr
  not not_43 (not_43_out, Q1);
  not not_44 (not_44_out, Q0);
  not not_45 (not_45_out, Q2_NEXT);
  not not_46 (not_46_out, Q1_NEXT);
  and and_38 (and_38_out, Q2, not_43_out, not_44_out);
  and and_39 (and_39_out, not_45_out, not_46_out, Q0_NEXT);
  and and_40 (and_40_out, and_38_out, and_39_out);
  Register #(.width(1)) register_4 (.D(1'b1), .en(and_40_out), .clk(CLK), .Q(DIN1));  // open: clr

  // Notes on the sheet:
  //   B11 to B0
  //   B0 to B1
  //   B1 to B0
  //   B00 to B1
endmodule

module BTXTEST (
  input  [11:0] in_1,
  input  in_2,
  input  in_3,
  input  in_4,
  input  in_5,
  output [31:0] out_6,
  output [24:0] out_7,
  output out_8,
  output [3:0] out_9,
  output out_10,
  output [7:0] out_11,
  output out_12,
  output [11:0] out_13,
  output [11:0] out_14,
  output out_15,
  output out_16,
  output out_17
);

  wire CLK, txrxd_1_din, txrxd_1_txout, vpwbtx_1_ser_out;

  Clock clock_1 (.out(CLK));
  VPWBRX vpwbrx_1 (
    .READ(in_4), .ENA(in_5), .CLK(CLK), .SER_IN(txrxd_1_din), .FRAME_OUT(out_13), .FULL(out_15),
    .EMPTY(out_16), .out_11(out_14), .out_10(out_17));  // open: CARE, ADDR
  VPWBTX vpwbtx_1 (
    .FRAME_IN(in_1), .WRITE(in_2), .ENA(in_3), .CLK(CLK), .SER_IN(txrxd_1_din), .FULL(out_10), .IDLE(out_12),
    .SER_OUT(vpwbtx_1_ser_out));
  TXRXD txrxd_1 (.DOUT(vpwbtx_1_ser_out), .RXIN(txrxd_1_txout), .DIN(txrxd_1_din), .TXOUT(txrxd_1_txout));
  Pull_Resistor #(.pull(1)) pull_resistor_1 (.node(txrxd_1_txout));
  VPWBMonitor vpwbmonitor_1 (
    .RXIN(txrxd_1_txout), .CLK(CLK), .LAST_FE(out_8), .LAST_ADDR(out_9), .LAST_DATA(out_11), .out_3(out_6),
    .out_4(out_7));
endmodule

module Observertest (
);

  wire and_1_out, CLK, DIN, IDLE, NEWBIT, NEWCHAR, PREVIDLE, RX;
  wire [4:0] counter_1_q;
  wire [6:0] CHAR_IN;

  D_Flip_Flop d_ff_1 (.D(IDLE), .clk(CLK), .Q(PREVIDLE));  // open: Qn, preset, reset
  Clock clock_1 (.out(CLK));
  TTY tty_1 (.data(CHAR_IN), .clk(CLK), .we(NEWCHAR));  // open: clr
  and and_1 (and_1_out, IDLE, ~PREVIDLE);  // AND_Gate
  or or_1 (NEWCHAR, and_1_out, NEWBIT);
  VPWBObserver vpwbobserver_1 (.ENA(1'b1), .CLK(CLK), .RX(RX), .DIN(DIN), .NEWBIT(NEWBIT), .IDLE(IDLE));
  ROM #(.addrWidth(5), .dataWidth(1)) rom_1 (.addr(counter_1_q), .data(RX));
  Counter #(.max('h1f), .width(5)) counter_1 (
    .count(1'b1), .Q(counter_1_q), .clk(CLK));  // open: load, D, carry, up, clr
  Multiplexer #(.select(2), .width(7)) multiplexer_1 (
    .in0(7'b0110000), .in1(7'b0110001), .in2(7'b1001001), .in3(7'b1001001), .out(CHAR_IN), .sel({IDLE, DIN}));

  // Notes on the sheet:
  //   contents of rom_1 (hex, n*v repeats v):
  //   0 0 1 0 1 1 0 0 1 0 1 1 0 1 0 0 1 1 0 0 1 1 1 0 1 0 0 1
endmodule

module ArbiterTest (
);

  wire and_1_out, BITCMP, CLK, not_1_out, SHIFT, shift_register_1_out, vpwbarbiter_1_tx;
  wire [3:0] counter_1_q;

  Clock clock_1 (.out(CLK));
  Shift_Register #(.length(13)) shift_register_1 (
    .shift(SHIFT), .in(1'b0), .clk(CLK), .out(shift_register_1_out));  // open: load, clr, d0, q0, d1, q1, d2, q2, d3, q3, d4, q4, d5, q5, d6, q6, d7, q7, d8, q8, d9, q9, d10, q10, d11, q11, d12, q12
  Counter #(.max('hd), .width(4)) counter_1 (
    .count(SHIFT), .Q(counter_1_q), .clk(CLK));  // open: load, D, carry, up, clr
  and and_1 (and_1_out, counter_1_q[0], ~counter_1_q[1], counter_1_q[2], counter_1_q[3]);  // AND_Gate
  not not_1 (not_1_out, counter_1_q[0]);
  and and_2 (SHIFT, BITCMP, ~and_1_out);  // AND_Gate
  VPWBArbiter vpwbarbiter_1 (
    .DW(SHIFT), .EVENBIT(not_1_out), .DOUT(shift_register_1_out), .ENA(1'b1), .CLK(CLK),
    .RX(vpwbarbiter_1_tx), .BITCMP(BITCMP), .TX(vpwbarbiter_1_tx));  // open: ARBL
  Shift_Register #(.length(24)) shift_register_2 (
    .shift(1'b1), .in(vpwbarbiter_1_tx), .clk(CLK));  // open: out, load, clr, d0, q0, d1, q1, d2, q2, d3, q3, d4, q4, d5, q5, d6, q6, d7, q7, d8, q8, d9, q9, d10, q10, d11, q11, d12, q12, d13, q13, d14, q14, d15, q15, d16, q16, d17, q17, d18, q18, d19, q19, d20, q20, d21, q21, d22, q22, d23, q23
endmodule
